// Logisim project complete_ALU.circ as structural Verilog: 1 circuit, main circuit main
module main (
  input  [1:0] in_1,
  input  [3:0] in_2,
  input  [3:0] in_3,
  input  _1___left,
  output [3:0] Output,
  output out_6,
  output out_7
);

  wire and_1_out, and_2_out, and_3_out, and_4_out, and_5_out, and_6_out, and_7_out, and_8_out, and_9_out,
       and_10_out, and_11_out, and_12_out, and_13_out, and_14_out, and_15_out, and_16_out, and_17_out,
       and_18_out, and_19_out, and_20_out, and_21_out, and_22_out, and_23_out, and_25_out, not_1_out,
       not_2_out, not_3_out, not_4_out, not_5_out, not_6_out, not_7_out, not_8_out, not_9_out, not_10_out,
       not_11_out, not_12_out, or_2_out, or_3_out, or_5_out, or_6_out, xor_1_out, xor_3_out, xor_5_out,
       xor_8_out, xor_10_out, xor_12_out, xor_15_out, xor_17_out, xor_18_out, xor_20_out, xor_21_out,
       xor_23_out, xor_24_out;
  wire [3:0] and_24_out, demultiplexer_1_out0, demultiplexer_1_out1, demultiplexer_1_out2,
       demultiplexer_1_out3, demultiplexer_2_out0, demultiplexer_2_out1, demultiplexer_2_out2,
       demultiplexer_2_out3, xor_7_out, xor_14_out, xor_25_out;

  or or_1 (out_6, and_1_out, and_2_out);
  and and_1 (and_1_out, demultiplexer_1_out0[3], demultiplexer_2_out0[3]);
  and and_2 (and_2_out, xor_1_out, or_2_out);
  Demultiplexer #(.select(2), .width(4)) demultiplexer_1 (
    .out0(demultiplexer_1_out0), .out1(demultiplexer_1_out1), .out2(demultiplexer_1_out2),
    .out3(demultiplexer_1_out3), .in(in_2), .sel(in_1));  // open: en
  or or_2 (or_2_out, and_4_out, and_3_out);
  xor xor_1 (xor_1_out, demultiplexer_2_out0[3], demultiplexer_1_out0[3]);
  xor xor_2 (xor_7_out[3], or_2_out, xor_1_out);
  Demultiplexer #(.select(2), .width(4)) demultiplexer_2 (
    .out0(demultiplexer_2_out0), .out1(demultiplexer_2_out1), .out2(demultiplexer_2_out2),
    .out3(demultiplexer_2_out3), .in(in_3), .sel(in_1));  // open: en
  and and_3 (and_3_out, xor_3_out, or_3_out);
  and and_4 (and_4_out, demultiplexer_1_out0[2], demultiplexer_2_out0[2]);
  and and_5 (and_5_out, in_1[0], in_1[1]);
  xor xor_3 (xor_3_out, demultiplexer_2_out0[2], demultiplexer_1_out0[2]);
  xor xor_4 (xor_7_out[2], or_3_out, xor_3_out);
  and and_6 (and_6_out, and_5_out, _1___left);
  or or_3 (or_3_out, and_7_out, and_8_out);
  and and_7 (and_7_out, demultiplexer_1_out0[1], demultiplexer_2_out0[1]);
  and and_8 (and_8_out, xor_5_out, and_9_out);
  xor xor_5 (xor_5_out, demultiplexer_2_out0[1], demultiplexer_1_out0[1]);
  xor xor_6 (xor_7_out[1], and_9_out, xor_5_out);
  and and_9 (and_9_out, demultiplexer_1_out0[0], demultiplexer_2_out0[0]);
  xor xor_7 (xor_7_out[0], demultiplexer_2_out0[0], demultiplexer_1_out0[0]);
  or or_4 (out_7, and_10_out, and_11_out);
  and and_10 (and_10_out, demultiplexer_1_out1[3], not_1_out);
  not not_1 (not_1_out, demultiplexer_2_out1[3]);
  not not_2 (not_2_out, xor_8_out);
  and and_11 (and_11_out, or_5_out, not_2_out);
  or or_5 (or_5_out, and_12_out, and_13_out);
  xor xor_8 (xor_8_out, demultiplexer_1_out1[3], demultiplexer_2_out1[3]);
  xor xor_9 (xor_14_out[3], xor_8_out, or_5_out);
  and and_12 (and_12_out, demultiplexer_1_out1[2], not_3_out);
  not not_3 (not_3_out, demultiplexer_2_out1[2]);
  not not_4 (not_4_out, xor_10_out);
  and and_13 (and_13_out, or_6_out, not_4_out);
  or or_6 (or_6_out, and_14_out, and_15_out);
  xor xor_10 (xor_10_out, demultiplexer_1_out1[2], demultiplexer_2_out1[2]);
  xor xor_11 (xor_14_out[2], xor_10_out, or_6_out);
  and and_14 (and_14_out, demultiplexer_1_out1[1], not_5_out);
  not not_5 (not_5_out, demultiplexer_2_out1[1]);
  not not_6 (not_6_out, xor_12_out);
  and and_15 (and_15_out, and_16_out, not_6_out);
  and and_16 (and_16_out, demultiplexer_1_out1[0], not_7_out);
  xor xor_12 (xor_12_out, demultiplexer_1_out1[1], demultiplexer_2_out1[1]);
  xor xor_13 (xor_14_out[1], xor_12_out, and_16_out);
  not not_7 (not_7_out, demultiplexer_2_out1[0]);
  xor xor_14 (xor_14_out[0], demultiplexer_1_out1[0], demultiplexer_2_out1[0]);
  not not_8 (not_8_out, demultiplexer_1_out2[3]);
  xor xor_15 (xor_15_out, not_8_out, 1'b0);
  xor xor_16 (xor_25_out[3], xor_17_out, xor_15_out);
  xor xor_17 (xor_17_out, and_17_out, xor_20_out);
  and and_17 (and_17_out, 1'b0, not_9_out);
  not not_9 (not_9_out, demultiplexer_1_out2[2]);
  xor xor_18 (xor_18_out, not_9_out, 1'b0);
  xor xor_19 (xor_25_out[2], xor_20_out, xor_18_out);
  xor xor_20 (xor_20_out, and_18_out, xor_23_out);
  and and_18 (and_18_out, 1'b0, not_10_out);
  not not_10 (not_10_out, demultiplexer_1_out2[1]);
  xor xor_21 (xor_21_out, not_10_out, 1'b0);
  xor xor_22 (xor_25_out[1], xor_23_out, xor_21_out);
  xor xor_23 (xor_23_out, and_19_out, 1'b0);
  and and_19 (and_19_out, 1'b1, not_11_out);
  not not_11 (not_11_out, demultiplexer_1_out2[0]);
  xor xor_24 (xor_24_out, not_11_out, 1'b1);
  xor xor_25 (xor_25_out[0], 1'b0, xor_24_out);
  not not_12 (not_12_out, and_6_out);
  and and_20 (and_20_out, demultiplexer_1_out3[3], not_12_out);
  buf or_7 (and_24_out[3], and_21_out);  // OR_Gate
  and and_21 (and_21_out, and_6_out, demultiplexer_1_out3[2]);
  and and_22 (and_22_out, demultiplexer_1_out3[2], not_12_out);
  or or_8 (and_24_out[2], and_20_out, and_23_out);
  and and_23 (and_23_out, and_6_out, demultiplexer_1_out3[1]);
  or or_9 (and_24_out[1], and_22_out, and_25_out);
  and and_24 (and_24_out[0], demultiplexer_1_out3[1], not_12_out);
  and and_25 (and_25_out, and_6_out, demultiplexer_1_out3[0]);
  Multiplexer #(.select(2), .width(4)) multiplexer_1 (
    .in0(xor_7_out), .in1(xor_14_out), .in2(xor_25_out), .in3(and_24_out), .out(Output), .sel(in_1));  // open: en

  // Notes on the sheet:
  //   Larger than 4-bits
  //   00 = Addition
  //   01 = Subtraction
  //   10 = Two's Compliment
  //   11 = Shift Left/Right
  //   0 = right
  //   Larger than 4-bits
endmodule
